// Logisim project logic-gates.circ as structural Verilog: 7 circuits, main circuit NOT
module NOT (
  input  in_1,
  output out_2
);

  not not_1 (out_2, in_1);
endmodule

module AND (
  input  in_1,
  input  in_2,
  output out_3
);

  and and_1 (out_3, in_1, in_2);
endmodule

module OR (
  input  in_1,
  input  in_2,
  output out_3
);

  or or_1 (out_3, in_1, in_2);
endmodule

module XOR (
  input  in_1,
  input  in_2,
  output out_3
);

  wire nand_1_out, or_1_out;

  or or_1 (or_1_out, in_1, in_2);
  nand nand_1 (nand_1_out, in_1, in_2);
  and and_1 (out_3, or_1_out, nand_1_out);
endmodule

module NAND (
  input  in_1,
  input  in_2,
  output out_3
);

  nand nand_1 (out_3, in_1, in_2);
endmodule

module MUX (
  input  Input_1,
  input  select_bit,
  input  Input_2,
  output out_4
);

  wire nand_1_out, nand_2_out, nand_3_out;

  nand nand_1 (nand_1_out, select_bit, select_bit);
  nand nand_2 (nand_2_out, Input_1, select_bit);
  nand nand_3 (nand_3_out, nand_1_out, Input_2);
  nand nand_4 (out_4, nand_2_out, nand_3_out);
endmodule

module DMUX (
  input  Input,
  input  Select_Bit,
  output out_3,
  output out_4
);

  wire nand_1_out, nand_2_out, nand_3_out;

  nand nand_1 (nand_1_out, Select_Bit, Select_Bit);
  nand nand_2 (nand_2_out, Input, nand_1_out);
  nand nand_3 (nand_3_out, Select_Bit, Input);
  nand nand_4 (out_3, nand_2_out, nand_2_out);
  nand nand_5 (out_4, nand_3_out, nand_3_out);
endmodule
